# Fritzing sketch Arduino_Uno_LED_8x8_led_matrix_art (saved by Fritzing 1.0.5)
breadboards: 1

parts:
  パーツ1 = Arduino Uno (Rev3)
  J1 = Header 3 [package=screwterminal-3.5mm-3_lock.007s]
  LED1 = 8x8 LED Matrix (red)

nets:
  N1: パーツ1.GND, J1.2
  N2: パーツ1.D2, J1.3
  N3: パーツ1.D6_PWM, LED1.D
  N4: パーツ1.5V, J1.1

custom parts:
  8x8 LED Matrix (red): 8x8 LED Matrix with I2C control (red)
